# Fritzing sketch pico_led_14 (saved by Fritzing 0.9.3b)

parts:
  Mod1 = Raspberry Pi Pico
  LED1 = smd LED [color="Yellow (595nm)" package="0805 [SMD]"]
  R1 = Resistor [tolerance=±5% resistance=220 package="2010 [SMD]"]

nets:
  N1: Mod1.pin_18, Mod1.pin_42, LED1.cathode
  N2: Mod1.pin_19, R1.Pin_1

custom parts:
  Raspberry Pi Pico: Raspberry Pi Pico. Based around the RP2040 microcontroller the Pico is a low cost microcontroller device bringing Raspberry Pi quality, cost, and easy of use to the microcontroller space. Jan 2021, Split part in to two versions: tht (this one) and SMD. This one will drill holes for a .1 in header in pcb to allow plugging in the module as well as providing pads to solder the module to the top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
