# Fritzing sketch distance_sensor (saved by Fritzing 0.9.10b)

parts:
  HC-SR04_Sensor_1 = HC-SR04 Ultrasonic Distance Sensor
  Mod1 = Raspberry Pi Pico

nets:
  N1: HC-SR04_Sensor_1.VCC, Mod1.pin_36
  N2: HC-SR04_Sensor_1.TRIG, Mod1.pin_5
  N3: HC-SR04_Sensor_1.ECHO, Mod1.pin_4
  N4: HC-SR04_Sensor_1.GND, Mod1.pin_3

notes:
  HC-SR04-P 3.3v version

custom parts:
  Raspberry Pi Pico: Raspberry Pi Pico. Based around the RP2040 microcontroller the Pico is a low cost microcontroller device bringing Raspberry Pi quality, cost, and easy of use to the microcontroller space. Jan 2021, Split part in to two versions: tht (this one) and SMD. This one will drill holes for a .1 in header in pcb to allow plugging in the module as well as providing pads to solder the module to the top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
