# Fritzing sketch robot (saved by Fritzing 0.9.3b)

parts:
  Mod1 = Raspberry Pi Pico
  M1 = DC Motor
  L298N1 = L298N DC motor driver
  M2 = DC Motor
  VCC1 = 4 x AAA Battery Mount

nets:
  N1: Mod1.pin_16, L298N1.IN1
  N2: Mod1.pin_17, L298N1.IN2
  N3: Mod1.pin_19, L298N1.IN3
  N4: Mod1.pin_20, L298N1.IN4
  N5: Mod1.pin_23, Mod1.pin_33, Mod1.pin_42, L298N1.GND, VCC1.-
  N6: M1.pin_1, L298N1.OUT4
  N7: M1.pin_2, L298N1.OUT3
  N8: L298N1.OUT1, M2.pin_2
  N9: L298N1.OUT2, M2.pin_1
  N10: L298N1.5V, VCC1.+

custom parts:
  Raspberry Pi Pico: Raspberry Pi Pico. Based around the RP2040 microcontroller the Pico is a low cost microcontroller device bringing Raspberry Pi quality, cost, and easy of use to the microcontroller space. Jan 2021, Split part in to two versions: tht (this one) and SMD. This one will drill holes for a .1 in header in pcb to allow plugging in the module as well as providing pads to solder the module to the top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
  L298N DC motor driver: 2x DC motor driver with 78M05 positive voltage regulator (7..35 V) L298N: max 46 V, 2 A Set 5 V Enable jumper to enable 5 V regultor (needed for the L298N) and +5 V output at screw terminal or supply external +5 V at screw terminal Set ENA and/or ENB to +5 V to enable motor permanently or supply ENA and/or ENB with PWM signal IN1 and IN2 set rotation directory for motor A (OUT1/OUT2) IN2 and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
